# Fritzing sketch ESP8266 (saved by Fritzing 0.9.3b)
breadboards: 1

parts:
  부품1 = Arduino Uno (Rev3)
  U1 = ESP8266 WiFi Module [part_number=ESP8266]

nets:
  N1: 부품1.D9_PWM, U1.RXD
  N2: 부품1.D10_PWM/SS, U1.TXD
  3V3: 부품1.3V3, U1.VCC, U1.CH_PD
  GND: 부품1.GND, U1.GND

custom parts:
  ESP8266 WiFi Module: Generic WiFi Module based on the ESP8266 with onboard PCB antenna and UART communications
